# Fritzing sketch device_scheme (saved by Fritzing 0.9.3b)

parts:
  Part2 = LilyPad XBee
  Part4 = Lilypad Power Supply
  U1 = XBee
  Part7 = LilyPad LED
  Part8 = LilyPad LED
  Part9 = LilyPad LED
  Part10 = LilyPad Temperature Sensor
  Part11 = Lilypad Arduino Board
  Part13 = Arduino Uno (Rev3) - ICSP

nets:
  N1: Part2.RX-I, Part11.MOSI/D11
  N2: Part2.VCC, Part4.+
  GND: Part2.GND, Part4.GND
  N3: Part2.TX-O, Part11.D10
  VCC: U1.VCC, Part13.5V
  N4: U1.pin2, Part13.D0/RX
  N5: U1.pin3, Part13.D1/TX
  GND_2: U1.GND, Part13.GND
  N6: Part7.+, Part11.A5
  N7: Part8.+, Part11.A4
  N8: Part9.+, Part11.A3
  VCC_2: Part10.VCC, Part11.VCC
  GND_3: Part10.GND, Part11.GND
  N9: Part10.VO, Part11.A0
